# Fritzing sketch ArduinoGPEGASoundBox (saved by Fritzing 0.9.6b)
breadboards: 1

parts:
  LED3 = LED - 5mm [color="Green (570nm)" current=0.030 package="5 mm [THT]"]
  LED4 = LED - 5mm [color="Red (633nm)" current=0.030 package="5 mm [THT]"]
  J1 = Piezo Speaker
  Microcontroller = Arduino Nano (Rev3.0) (ICSP)
  ShiftRegister = SHIFT REGISTER [package=dil16]
  S1 = Pushbutton [package="[THT]"]
  LED5 = LED - 5mm [color="Red (633nm)" current=0.030 package="5 mm [THT]"]
  LED6 = LED - 5mm [color="Red (633nm)" current=0.030 package="5 mm [THT]"]
  R3 = Resistor [tolerance=±1% power=0.25 resistance=10k package=THT]
  R5 = Resistor [tolerance=±1% power=0.25 resistance=10k package=THT]
  R2 = Resistor [tolerance=±1% power=0.25 resistance=220 package=THT]
  R1 = Resistor [tolerance=±1% power=0.25 resistance=220 package=THT]
  R6 = Resistor [tolerance=±1% power=0.25 resistance=220 package=THT]
  R7 = Rotary Potentiometer (Large) [maximum_resistance=10kΩ package=THT]

nets:
  GND: LED3.cathode, LED4.cathode, J1.pin1, Microcontroller.GND, ShiftRegister.GND, ShiftRegister.G, LED6.cathode, R5.Pin_0, R7.leg2
  N1: LED3.anode, R3.Pin_0
  N2: LED4.anode, R2.Pin_1
  N3: J1.pin2, LED5.cathode
  N4: Microcontroller.D5, S1.Pin_1, S1.Pin_2, R5.Pin_1
  N5: Microcontroller.D6, ShiftRegister.SER
  N6: Microcontroller.D7, ShiftRegister.RCK
  N7: Microcontroller.D8, ShiftRegister.SCK
  5V: Microcontroller.5V, ShiftRegister.SCL, ShiftRegister.VCC, S1.Pin_3, S1.Pin_4, R7.leg1
  N8: Microcontroller.A0, R7.wiper
  N9: Microcontroller.D13/SCK, R6.Pin_0
  N10: ShiftRegister.QB, R2.Pin_0
  N11: ShiftRegister.QC, R3.Pin_1
  N12: ShiftRegister.QA, R1.Pin_0
  N13: LED5.anode, R6.Pin_1
  N14: LED6.anode, R1.Pin_1

// code stored in the sketch: arduino-gpega-soundbox.ino
#include "notes.h"

// HW
int KNOB_PIN   = A0;    // select the input pin for the potentiometer
int BUZZ_PIN   = 13;    // select the pin for the LED
int BUTTON_PIN = 5;
int DATA_PIN   = 7;     // Data pin (SER) of 74HC595 is connected to Digital pin 7
int LATCH_PIN  = 8;     // Latch pin (RCLK) of 74HC595 is connected to Digital pin 8
int CLOCK_PIN  = 9;     // Clock pin (SRCLK) of 74HC595 is connected to Digital pin 9

// SW
#define REST_NOTE 0

#define SEMIBREVE      240000
#define MINIM          SEMIBREVE / 2
#define CROTCHET       MINIM / 2
#define QUAVER         CROTCHET / 2
#define SEMIQUAVER     QUAVER / 2

// Tempo of the theme
byte tempo = 160;

byte leds = 0;         // Variable to hold the pattern of which LEDs are currently turned on or off
byte buttonValue = 0;
int  knobValue   = 0;  // variable to store the value coming from the sensor
int  gearcpt     = 0;

void buzz(int buzzer_pin, long freq, long length) {
  long delay_us = 1000000 / freq / 2;
  long nbCycles = freq * length / 1000;

  for (long i = 0; i < nbCycles; i++)
  {
    digitalWrite(buzzer_pin, HIGH);
    delayMicroseconds(delay_us);
    digitalWrite(buzzer_pin, LOW);
    delayMicroseconds(delay_us);
  }
}

void play_note(float note, float length){
  if (tempo) length = length / tempo;

  if (note != REST_NOTE)
  {
    buzz(BUZZ_PIN, note, length);
  }
  else
  {
    delay(length);
  }
}

void theme_pattern(int times, int pitch)
{
  for (int i = 0; i < times; i++)
  {
    play_note(notes[NOTE_FS2 + pitch], QUAVER);
    play_note(notes[NOTE_CS3 + pitch], QUAVER);
    play_note(notes[NOTE_FS3 + pitch], QUAVER);
    play_note(notes[NOTE_FS2 + pitch], QUAVER);
    play_note(notes[NOTE_E3  + pitch], QUAVER);
    play_note(notes[NOTE_FS2 + pitch], SEMIQUAVER);
    play_note(notes[NOTE_DS3 + pitch], QUAVER);
    play_note(notes[NOTE_FS2 + pitch], SEMIQUAVER);
    play_note(notes[NOTE_CS3 + pitch], QUAVER);
  }
}

void theme()
{
  theme_pattern(4, 0);
  theme_pattern(4, 12);
  theme_pattern(2, 12 + 5);
  theme_pattern(2, 12);
  theme_pattern(1, 7);
  theme_pattern(1, 12 + 5);
  theme_pattern(2, 12);
}

void boitier()
{
  int newVal = digitalRead(BUTTON_PIN);
  if (newVal != buttonValue)
  {
    if (newVal == 1)  gearcpt++;
    if (gearcpt == 6) gearcpt = 0;

    buttonValue = newVal;
  }
}

void vroum()
{
  int len = 50;
  // read the value from the sensor:
  knobValue = analogRead(KNOB_PIN);
  boitier();
  int buzz_freq = (knobValue * 1) - (gearcpt * 100);
  if (buzz_freq < 0) buzz_freq = 0;
  Serial.println(buzz_freq);
  // turn the BUZZ_PIN on
  buzz(BUZZ_PIN, buzz_freq, len);
  delay(len);
}

void updateShiftRegister()
{
  digitalWrite(LATCH_PIN, LOW);
  shiftOut(DATA_PIN, CLOCK_PIN, MSBFIRST, leds);
  digitalWrite(LATCH_PIN, HIGH);
}

void top_depart()
{
  int len = 500;

  leds = 0;
  updateShiftRegister();
  delay(len);

  leds = 0b001;
  updateShiftRegister();
  buzz(BUZZ_PIN, notes[NOTE_C4], len);
  delay(len);

  leds = 0b011;
  updateShiftRegister();
  buzz(BUZZ_PIN, notes[NOTE_C4], len);
  delay(len);

  leds = 0b111;
  updateShiftRegister();
  buzz(BUZZ_PIN, notes[NOTE_C5], len);
  delay(len);

  leds = 0;
  updateShiftRegister();
}

void setup() {
  Serial.begin(115200);

  // declare the BUZZ_PIN as an OUTPUT:
  pinMode(BUZZ_PIN, OUTPUT);
  // Set all the pins of 74HC595 as OUTPUT
  pinMode(LATCH_PIN, OUTPUT);
  pinMode(DATA_PIN,  OUTPUT);
  pinMode(CLOCK_PIN, OUTPUT);

  pinMode(BUTTON_PIN,  INPUT);

  updateShiftRegister();
  
  theme();
  top_depart();
}

void loop() {
  vroum();
}

// code stored in the sketch: GPEGA.ino
#include "notes.h"

// HW
int KNOB_PIN   = A0;    // select the input pin for the potentiometer
int BUZZ_PIN   = 13;    // select the pin for the LED
int BUTTON_PIN = 5;
int DATA_PIN   = 7;     // Data pin (SER) of 74HC595 is connected to Digital pin 7
int LATCH_PIN  = 8;     // Latch pin (RCLK) of 74HC595 is connected to Digital pin 8
int CLOCK_PIN  = 9;     // Clock pin (SRCLK) of 74HC595 is connected to Digital pin 9

// SW
#define REST_NOTE 0

#define SEMIBREVE      240000
#define MINIM          SEMIBREVE / 2
#define CROTCHET       MINIM / 2
#define QUAVER         CROTCHET / 2
#define SEMIQUAVER     QUAVER / 2

// Tempo of the theme
byte tempo = 160;

byte leds = 0;         // Variable to hold the pattern of which LEDs are currently turned on or off
byte buttonValue = 0;
int  knobValue   = 0;  // variable to store the value coming from the sensor
int  gearcpt     = 0;

void buzz(int buzzer_pin, long freq, long length) {
  long delay_us = 1000000 / freq / 2;
  long nbCycles = freq * length / 1000;

  for (long i = 0; i < nbCycles; i++)
  {
    digitalWrite(buzzer_pin, HIGH);
    delayMicroseconds(delay_us);
    digitalWrite(buzzer_pin, LOW);
    delayMicroseconds(delay_us);
  }
}

void play_note(float note, float length){
  if (tempo) length = length / tempo;

  if (note != REST_NOTE)
  {
    buzz(BUZZ_PIN, note, length);
  }
  else
  {
    delay(length);
  }
}

void theme_pattern(int times, int pitch)
{
  for (int i = 0; i < times; i++)
  {
    play_note(notes[NOTE_FS2 + pitch], QUAVER);
    play_note(notes[NOTE_CS3 + pitch], QUAVER);
    play_note(notes[NOTE_FS3 + pitch], QUAVER);
    play_note(notes[NOTE_FS2 + pitch], QUAVER);
    play_note(notes[NOTE_E3  + pitch], QUAVER);
    play_note(notes[NOTE_FS2 + pitch], SEMIQUAVER);
    play_note(notes[NOTE_DS3 + pitch], QUAVER);
    play_note(notes[NOTE_FS2 + pitch], SEMIQUAVER);
    play_note(notes[NOTE_CS3 + pitch], QUAVER);
  }
}

void theme()
{
  theme_pattern(4, 0);
  theme_pattern(4, 12);
  theme_pattern(2, 12 + 5);
  theme_pattern(2, 12);
  theme_pattern(1, 7);
  theme_pattern(1, 12 + 5);
  theme_pattern(2, 12);
}

void boitier()
{
  int newVal = digitalRead(BUTTON_PIN);
  if (newVal != buttonValue)
  {
    if (newVal == 1)  gearcpt++;
    if (gearcpt == 6) gearcpt = 0;

    buttonValue = newVal;
  }
}

void vroum()
{
  int len = 50;
  // read the value from the sensor:
  knobValue = analogRead(KNOB_PIN);
  boitier();
  int buzz_freq = (knobValue * 1) - (gearcpt * 100);
  if (buzz_freq < 0) buzz_freq = 0;
  Serial.println(buzz_freq);
  // turn the BUZZ_PIN on
  buzz(BUZZ_PIN, buzz_freq, len);
  delay(len);
}

void updateShiftRegister()
{
  digitalWrite(LATCH_PIN, LOW);
  shiftOut(DATA_PIN, CLOCK_PIN, MSBFIRST, leds);
  digitalWrite(LATCH_PIN, HIGH);
}

void top_depart()
{
  int len = 500;

  leds = 0;
  updateShiftRegister();
  delay(len);

  leds = 0b001;
  updateShiftRegister();
  buzz(BUZZ_PIN, notes[NOTE_C4], len);
  delay(len);

  leds = 0b011;
  updateShiftRegister();
  buzz(BUZZ_PIN, notes[NOTE_C4], len);
  delay(len);

  leds = 0b111;
  updateShiftRegister();
  buzz(BUZZ_PIN, notes[NOTE_C5], len);
  delay(len);

  leds = 0;
  updateShiftRegister();
}

void setup() {
  Serial.begin(115200);

  // declare the BUZZ_PIN as an OUTPUT:
  pinMode(BUZZ_PIN, OUTPUT);
  // Set all the pins of 74HC595 as OUTPUT
  pinMode(LATCH_PIN, OUTPUT);
  pinMode(DATA_PIN,  OUTPUT);
  pinMode(CLOCK_PIN, OUTPUT);

  pinMode(BUTTON_PIN,  INPUT);

  updateShiftRegister();
  
  theme();
  top_depart();
}

void loop() {
  vroum();
}
